# Fritzing sketch Labirinto (saved by Fritzing 0.9.3b)
breadboards: 1

parts:
  Componente1 = Arduino Uno (Rev3)
  Componente2 = Thumb Joystick
  J1 = Basic Servo
  J2 = Basic Servo

nets:
  N1: Componente1.A4/SDA, Componente2.HORZ
  N2: Componente1.A5/SCL, Componente2.VERT
  N3: Componente1.D10_PWM/SS, J2.pulse
  N4: Componente1.D11_PWM/MOSI, J1.pulse
  VCC: Componente1.5V, Componente2.VCC, J1.vcc, J2.vcc
  GND: Componente1.GND, Componente2.GND, J1.gnd, J2.gnd
